# Fritzing sketch btw_breadboard (saved by Fritzing 0.8.4b)
breadboards: 1

parts:
  R1 = Resistor [tolerance=±5% resistance=220 package=THT]
  LED2 = LED - 5mm [color="Red (633nm)" package="5 mm [THT]"]
  R2 = Resistor [tolerance=±5% resistance=220 package=THT]
  R3 = Resistor [tolerance=±5% resistance=220 package=THT]
  LED3 = LED - 5mm [color="Yellow (595nm)" package="5 mm [THT]"]
  LED4 = LED - 5mm [color="Green (570nm)" package="5 mm [THT]"]
  Q1 = NPN-Transistor [part_number=2n2222a package="TO92 [THT]"]
  R4 = Resistor [tolerance=±5% resistance=350 package=THT]
  R5 = Resistor [tolerance=±5% resistance=350 package=THT]
  D1 = Rectifier Diode [part_number=1N4001 package="300 mil [THT]"]
  R6 = Resistor [tolerance=±5% resistance=350 package=THT]
  J1 = Basic Servo
  M1 = DC Motor
  S1 = Pushbutton [package="[THT]"]
  S2 = Pushbutton [package="[THT]"]
  R7 = Rotary Potentiometer (Small) [maximum_resistance=100kΩ package=THT]
  Part3 = Arduino Uno (Rev3)

nets (from the schematic view):
  N1: R1.Pin_0, Part3.D0/RX
  N2: R1.Pin_1, LED2.anode
  GND: LED2.cathode, LED3.cathode, LED4.cathode, Q1.E, J1.gnd, S1.Pin_1, S1.Pin_2, S2.Pin_1, S2.Pin_2, R7.leg2, Part3.GND
  N3: R2.Pin_0, Part3.D2
  N4: R2.Pin_1, LED3.anode
  N5: R3.Pin_0, Part3.D4
  N6: R3.Pin_1, LED4.anode
  N7: Q1.B, R6.Pin_1
  N8: Q1.C, D1.anode, M1.pin_1
  N9: R4.Pin_0, S1.Pin_3, S1.Pin_4, Part3.D6_PWM
  VCC: R4.Pin_1, R5.Pin_1, D1.cathode, J1.vcc, M1.pin_2, R7.leg1, Part3.5V
  N10: R5.Pin_0, S2.Pin_3, S2.Pin_4, Part3.D8
  N11: R6.Pin_0, Part3.D10_PWM/SS
  N12: J1.pulse, Part3.D11_PWM/MOSI
  N13: R7.wiper, Part3.A1

notes:
  Behind The Wire, Prototyping shield schematic to replicate the original BTW circuit, 1.0
