# Fritzing sketch btw_arduino_shield (saved by Fritzing 0.8.4b)

parts:
  Arduino_Pinout = Arduino Prototyping Shield
  R1 = Resistor [tolerance=±5% resistance=220 package=THT]
  LED2 = LED - 5mm [color="Red (633nm)" package="5 mm [THT]"]
  R2 = Resistor [tolerance=±5% resistance=220 package=THT]
  R3 = Resistor [tolerance=±5% resistance=220 package=THT]
  LED3 = LED - 5mm [color="White (4500K)" package="5 mm [THT]"]
  LED4 = LED - 5mm [color="Green (570nm)" package="5 mm [THT]"]
  Q1 = NPN-Transistor [part_number=2n2222a package="TO92 [THT]"]
  Servo_Out = Header 3 [package=molex-1x3_lock]
  R4 = Resistor [tolerance=±5% resistance=350 package=THT]
  R5 = Resistor [tolerance=±5% resistance=350 package=THT]
  D1 = Rectifier Diode [part_number=1N4001 package="300 mil [THT]"]
  Pot_out = Header 3 [package=molex-1x3_lock]
  Motor_out_Left = Header 2 [package=molex-1x2_lock]
  R6 = Resistor [tolerance=±5% resistance=350 package=THT]
  Buttons_Left_Right_Out = Header 3 [package=molex-1x3_lock]
  J1 = Basic Servo
  Motor_Right = DC Motor
  S1 = Pushbutton [package="[THT]"]
  S2 = Pushbutton [package="[THT]"]
  R7 = Rotary Potentiometer (Small) [maximum_resistance=100kΩ package=THT]
  Pot_in = Header 3 [package=molex-1x3_lock]
  LEDs_Out = Header 4 [package=molex-1x4_lock]
  LEDs_In = Header 4 [package=molex-1x4_lock]
  Buttons_Left_Right_In = Header 3 [package=molex-1x3_lock]
  Servo_In = Header 3 [package=molex-1x3_lock]
  R8 = Resistor [tolerance=±5% resistance=350 package=THT]
  Q2 = NPN-Transistor [part_number=2n2222a package="TO92 [THT]"]
  D2 = Rectifier Diode [part_number=1N4001 package="300 mil [THT]"]
  Motor_out_Right = Header 2 [package=molex-1x2_lock]
  Motor_In_Left = Header 2 [package=molex-1x2_lock]
  Motor_In_Right = Header 2 [package=molex-1x2_lock]
  C1 = Tantalum Capacitor [capacitance=1μF package="100 mil [THT, tantalum]"]
  Motor_Left = DC Motor
  C2 = Tantalum Capacitor [capacitance=1μF package="100 mil [THT, tantalum]"]

nets:
  N1: Arduino_Pinout.A2, Arduino_Pinout.N$326, R4.Pin_1, Buttons_Left_Right_Out.3
  N2: Arduino_Pinout.A3, Arduino_Pinout.N$323, R5.Pin_1, Buttons_Left_Right_Out.1
  N3: Arduino_Pinout.+5V, Arduino_Pinout.N$75, Arduino_Pinout.N$327, Arduino_Pinout.N$401, Arduino_Pinout.N$408, Servo_Out.3, R4.Pin_0, R5.Pin_0, D1.cathode, Pot_out.3, Motor_out_Left.1, D2.cathode, Motor_out_Right.1
  N4: Arduino_Pinout.GND, Arduino_Pinout.N$178, Arduino_Pinout.N$190, Arduino_Pinout.N$241, Arduino_Pinout.N$332, Arduino_Pinout.N$368, Arduino_Pinout.N$369, Q1.E, Servo_Out.1, Pot_out.2, Buttons_Left_Right_Out.2, LEDs_Out.4, Q2.E
  N5: Arduino_Pinout.D3, Arduino_Pinout.N$232, R6.Pin_0
  N6: Arduino_Pinout.D10, Arduino_Pinout.N$48, Arduino_Pinout.N$49, R1.Pin_1
  N7: Arduino_Pinout.D11, Arduino_Pinout.N$74, Servo_Out.2
  N8: Arduino_Pinout.D5, R8.Pin_0
  N9: Arduino_Pinout.A0, Arduino_Pinout.N$27, Arduino_Pinout.N$28, R3.Pin_0
  N10: Arduino_Pinout.A1, Arduino_Pinout.N$36, Arduino_Pinout.N$37, R2.Pin_0
  N11: Arduino_Pinout.A5, Arduino_Pinout.N$81, Pot_out.1
  N12: Arduino_Pinout.N$34, R3.Pin_1, LEDs_Out.3
  N13: Arduino_Pinout.N$41, R2.Pin_1, LEDs_Out.2
  N14: Arduino_Pinout.N$55, R1.Pin_0, LEDs_Out.1
  N15: Arduino_Pinout.N$311, Arduino_Pinout.N$312, Q1.B, R6.Pin_1
  N16: Arduino_Pinout.N$313, Arduino_Pinout.N$404, Q1.C, D1.anode, Motor_out_Left.2
  N17: LED2.cathode, LED3.cathode, LED4.cathode, LEDs_In.4
  N18: LED2.anode, LEDs_In.3
  N19: LED3.anode, LEDs_In.2
  N20: LED4.anode, LEDs_In.1
  N21: J1.gnd, Servo_In.1
  N22: J1.vcc, Servo_In.3
  N23: J1.pulse, Servo_In.2
  N24: Motor_Right.pin_1, Motor_In_Right.2, C1.-
  N25: Motor_Right.pin_2, Motor_In_Right.1, C1.+
  N26: S1.Pin_1, S1.Pin_2, Buttons_Left_Right_In.3
  N27: S1.Pin_3, S1.Pin_4, S2.Pin_3, S2.Pin_4, Buttons_Left_Right_In.2
  N28: S2.Pin_1, Buttons_Left_Right_In.1
  N29: R7.leg1, Pot_in.2
  N30: R7.wiper, Pot_in.3
  N31: R7.leg2, Pot_in.1
  N32: R8.Pin_1, Q2.B
  N33: Q2.C, D2.anode, Motor_out_Right.2
  N34: Motor_In_Left.1, Motor_Left.pin_1, C2.-
  N35: Motor_In_Left.2, Motor_Left.pin_2, C2.+

notes:
  Behind The Wire, Prototyping shield schematic to use with the BTW source code, 1.0
